// Logisim project alu.circ as structural Verilog: 3 circuits, main circuit alu
module alu (
  input  [31:0] A,
  input  [31:0] B,
  input  [3:0] ALUSel,
  output [31:0] Result
);


  // Notes on the sheet:
  //   INPUTS to your circuit
  //   DON'T CHANGE THE LOCATIONS OF THE INPUTS AND OUTPUTS!
  //   OUTPUT from your circuit
endmodule

module add (
  input  [31:0] A,
  input  [31:0] B,
  output [31:0] Result
);

  Adder #(.width(32)) adder_1 (.a(A), .b(B), .out(Result));  // open: cin, cout
endmodule

module sub (
  input  [31:0] A,
  input  [31:0] B,
  output [31:0] Result
);

  Subtractor #(.width(32)) subtractor_1 (.a(A), .b(B), .out(Result));  // open: bin, bout
endmodule
